// Logisim project ULA4_core.circ as structural Verilog: 1 circuit, main circuit main
module main (
  input  [3:0] in_1,
  input  in_2,
  input  [3:0] in_3,
  input  in_4,
  input  [3:0] in_5,
  input  in_6,
  output [7:0] out_7
);
endmodule
